# Fritzing sketch ARCAFritz (saved by Fritzing 0.9.3b)
breadboards: 1

parts:
  8x8_LED_Modul_mit_MAX1 = 8x8 LED Modul mit MAX7219 [package=THT]
  8x8_LED_Modul_mit_MAX2 = 8x8 LED Modul mit MAX7219 [package=THT]
  Q1 = TIP120 Hi-Current Darlington Transistor
  Q2 = TIP120 Hi-Current Darlington Transistor
  Part1 = Arduino Uno (Rev3)
  M1 = DC Motor
  M2 = DC Motor
  IR1 = TSOP312.., 314.. [package=THT]
  R1 = Resistor [tolerance=±5% resistance=220 package=THT]  # not connected

nets:
  N1: 8x8_LED_Modul_mit_MAX1.VCC_Eingang, 8x8_LED_Modul_mit_MAX2.VCC_Eingang, Part1.5V
  N2: 8x8_LED_Modul_mit_MAX1.GND_Eingang, 8x8_LED_Modul_mit_MAX2.GND_Eingang, Q1.EMITTER, Q2.EMITTER, Part1.GND, M1.pin_2, M2.pin_2, IR1.Vs
  N3: 8x8_LED_Modul_mit_MAX1.DIN_Eingang, Part1.D7
  N4: 8x8_LED_Modul_mit_MAX1.CS_Eingang, Part1.D6_PWM
  N5: 8x8_LED_Modul_mit_MAX1.CLK_Eingang, Part1.D5_PWM
  N6: 8x8_LED_Modul_mit_MAX2.DIN_Eingang, Part1.D10_PWM/SS
  N7: 8x8_LED_Modul_mit_MAX2.CS_Eingang, Part1.D9_PWM
  N8: Q1.BASE, Part1.D3_PWM
  N9: Q1.COLLECTOR, M1.pin_1
  N10: Q2.BASE, Part1.D2
  N11: Q2.COLLECTOR, M2.pin_1
  N12: Part1.D11_PWM/MOSI, IR1.GND
